# Fritzing sketch Fritzing sketch (saved by Fritzing 0.9.3b)

parts:
  Part1 = LCD Keypad Shield
  Part2 = HX711 Weighing Sensor Module
  Load_Cell1 = Load Cell - Red/white/black/green

nets:
  N1: Part1.D2, Part2.DO/RX
  N2: Part1.D3, Part2.CK/TX
  +5V: Part1.+5V, Part2.VCC
  GND: Part1.GND, Part2.GND
  N3: Part2.E+, Load_Cell1.wire1
  N4: Part2.E-, Load_Cell1.wire3
  N5: Part2.A+, Load_Cell1.wire2
  N6: Part2.A-, Load_Cell1.wire4

custom parts:
  LCD Keypad Shield: It consists of a 1602 white character blue backlight LCD. The keypad consists of 5 keys — select, up, right, down and left. To save the digital IO pins, the keypad interface uses only one ADC channel. The key value is read through a 5 stage voltage divider.
  Load Cell - Red/white/black/green: A rectangle load cell/weighting pressure Sensor with four wires - Red, white, black, green. Normally corresponding with E+, E-, A+, A- respectively.
